# Fritzing sketch BREADBOARD (saved by Fritzing 0.9.3b)
breadboards: 1
perfboards: 1

parts:
  Bauteil1 = Arduino Uno (Rev3)
  U5 = 74HC4052 [package=dil16]
  U9 = 74HC4052 [package=dil16]
  U10 = 74HC4052 [package=dil16]
  U11 = 74HC4052 [package=dil16]
  U13 = 74HC4052 [package=dil16]
  U14 = 74HC4052 [package=dil16]
  U8 = 74HC4052 [package=dil16]
  U1 = 74HC4052 [package=dil16]

nets:
  N1: Bauteil1.A0, U1.Y
  N2: Bauteil1.A3, U5.X0
  N3: Bauteil1.A4/SDA, U5.X3
  N4: Bauteil1.A5/SCL, U5.A
  N5: Bauteil1.D8, U10.X3, U14.X3, U8.X3
  N6: Bauteil1.D9_PWM, U10.A, U14.A, U8.A
  N7: Bauteil1.D10_PWM/SS, U10.B, U14.B, U8.B
  N8: Bauteil1.D11_PWM/MOSI, U9.X3, U11.X3, U1.X3
  N9: Bauteil1.D12/MISO, U9.A, U11.A, U1.A
  N10: Bauteil1.D13/SCK, U9.B, U11.B, U1.B
  N11: Bauteil1.D1/TX, U9.Y
  N12: Bauteil1.D3_PWM, U13.Y
  N13: Bauteil1.D4, U11.Y
  N14: Bauteil1.D5_PWM, U13.X3
  N15: Bauteil1.D6_PWM, U13.A
  N16: Bauteil1.D7, U13.B
  N17: U5.Y, U13.X
  GND: U5.INH, U5.VEE, U5.GND, U9.INH, U9.VEE, U9.GND, U10.INH, U10.VEE, U10.GND, U11.INH, U11.VEE, U11.GND, U13.INH, U13.VEE, U13.GND, U14.INH, U14.VEE, U14.GND, U8.INH, U8.VEE, U8.GND, U1.INH, U1.VEE, U1.GND
  VCC: U5.VCC, U9.VCC, U10.VCC, U11.VCC, U13.VCC, U14.VCC, U8.VCC, U1.VCC
  N18: U9.X, U8.Y
  N19: U10.Y, U1.X
  N20: U11.X, U14.Y

notes:
  A
  B
  D
  C
  A1
  B1
  D1
  C1
